# Fritzing sketch andruino_demov4 (saved by Fritzing 0.9.2b)
breadboards: 1

parts:
  Part1 = Arduino Uno (Rev3)
  U1 = mystery part, 4 pins [chip_label=Bluetooth]
  R1 = Resistor [tolerance=±5% resistance=10k package=THT]
  R2 = Resistor [tolerance=±5% resistance=10k package=THT]
  R3 = Resistor [tolerance=±5% resistance=10k package=THT]
  U2 = mystery part, 4 pins [chip_label=GPS]
  U3 = mystery part, 6 pins [chip_label="SD Logger"]

nets:
  N1: Part1.D10_PWM/SS, U3.pin1
  N2: Part1.D11_PWM/MOSI, U3.pin3
  N3: Part1.D12/MISO, U3.pin4
  N4: Part1.D13/SCK, U3.pin2
  N5: Part1.D0/RX, U1.pin3
  N6: Part1.D1/TX, U1.pin4, R1.Pin_0
  N7: Part1.D2, U2.pin2
  N8: Part1.D3_PWM, U2.pin3
  N9: Part1.5V, U1.pin1, U2.pin1, U2.pin4, U3.pin5
  N10: Part1.GND, U1.pin2, R2.Pin_1, R3.Pin_1, U3.pin6
  N11: R1.Pin_1, R2.Pin_0, R3.Pin_0

notes:
  Goes with arduino_demov4.ino. Does not include LEDs on pins 7 and 9.
